# Fritzing sketch wiring_diagram (saved by Fritzing 0.9.6b)
stripboards: 2

parts:
  S2 = Pushbutton [package="[THT]"]
  Part3 = Itsy Bitsy 32u4 3V @ 8MHz [part_number="Adafruit 3675"]
  OLED2 = OLED 128x64 I2C Monochrome Display GND-VDD
  ENCODER3 = Rotary Encoder with Knob
  ENCODER4 = Rotary Encoder with Knob
  Q2 = LTR-301 [package=ltr-301]
  R2 = Resistor [tolerance=±5% power=0.25 resistance=1k package=THT]

nets:
  N1: S2.Pin_1, S2.Pin_2, Part3.D0
  GND: S2.Pin_3, S2.Pin_4, Part3.GND, OLED2.GND, ENCODER3.no_name_yet#2, ENCODER3.no_name_yet#4, ENCODER4.no_name_yet#2, ENCODER4.no_name_yet#4, R2.Pin_1
  N2: Part3.D12, Q2.E, R2.Pin_0
  N3: Part3.D11, ENCODER4.no_name_yet#5
  N4: Part3.D10, ENCODER4.no_name_yet#3
  N5: Part3.D9, ENCODER3.no_name_yet#5
  N6: Part3.SCL, OLED2.SCK
  N7: Part3.SDA, OLED2.SDA
  N8: Part3.MISO, ENCODER3.no_name_yet#3
  N9: Part3.MOSI, ENCODER3.no_name_yet#1
  N10: Part3.SCK, ENCODER4.no_name_yet#1
  +3V3: Part3.+3V3, OLED2.VDD, Q2.C

notes:
  Hot Shoe
  Ground
  3.3V

custom parts:
  Itsy Bitsy 32u4 3V @ 8MHz: What's smaller than a Feather but larger than a Trinket? It's an Itsy Bitsy! Small, powerful, Arduino-compatible - this microcontroller board is perfect when you want something very compact, but still with a bunch of pins. Itsy Bitsy is only 1.4" long by 0.7" wide, but has 6 power pins, 6 analog & digital pins and 17 digital pins. It packs much of the same capability as an Arduino UNO or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
  OLED 128x64 I2C Monochrome Display GND-VDD: OLED 128x64 I2C Monochrome Display. Note: there are two variants of this part, this one is the GND VDD SCK SDA variant. The other is VDD GND SCK SDA. Make sure you select the part that matches your module as using the incorrect part will probably destroy your module! In addition the mounting holes are marked on silkscreen but not by default drilled. If you want drilled mounting holes, copy a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
  Rotary Encoder with Knob: Rotary Encoder with 1/4" Shaft and Knob
