# Fritzing sketch wiring_diagram_breadboard (saved by Fritzing 0.9.6b)
stripboards: 2

parts:
  Part1 = Itsy Bitsy 32u4 3V @ 8MHz [part_number="Adafruit 3675"]
  J1 = female pin header, 11 pins [form="♀ (female)"]
  J2 = female pin header, 10 pins [form="♀ (female)"]
  J3 = female pin header, 11 pins [form="♀ (female)"]
  J4 = female pin header, 10 pins [form="♀ (female)"]
  OLED1 = OLED 128x64 I2C Monochrome Display GND-VDD
  ENCODER1 = Rotary Encoder with Knob
  ENCODER2 = Rotary Encoder with Knob
  U1 = LIPO-110mAh [package=lipo-110]
  Part2 = Micro Lipo Charger
  Q1 = LTR-301 [package=ltr-301]
  S1 = Pushbutton [package="[THT]"]
  J5 = female pin header, 4 pins [form="♀ (female)"]
  R1 = Resistor [tolerance=±5% power=0.25 resistance=2.2k package=THT]

nets:
  N1: Part1.VBAT, Part2.VBAT
  GND: Part1.GND, J2.pin10, J4.pin10, OLED1.GND, ENCODER1.no_name_yet#2, ENCODER1.no_name_yet#4, ENCODER2.no_name_yet#2, ENCODER2.no_name_yet#5, Part2.GND, S1.Pin_1, S1.Pin_2, J5.pin2, R1.Pin_1
  N2: Part1.VBUS, Part2.5V
  N3: Part1.D13, J1.pin1
  N4: Part1.D12, J1.pin2, Q1.E, J5.pin3, R1.Pin_0
  N5: Part1.D11, J1.pin3, ENCODER1.no_name_yet#5
  N6: Part1.D10, J1.pin4, ENCODER1.no_name_yet#3
  N7: Part1.D9, J1.pin5, ENCODER2.no_name_yet#4
  N8: Part1.D7, J1.pin6
  N9: Part1.D5_OUT, J1.pin7, J3.pin7
  N10: Part1.SCL, J1.pin8, OLED1.SCK
  N11: Part1.SDA, J1.pin9, J3.pin9, OLED1.SDA
  N12: Part1.D1, J1.pin10, J3.pin10
  N13: Part1.D0, J1.pin11, J3.pin11, S1.Pin_3, S1.Pin_4, J5.pin1
  N14: Part1.MISO, J2.pin9, J4.pin9, ENCODER2.no_name_yet#3
  N15: Part1.MOSI, J2.pin8, J4.pin8, ENCODER2.no_name_yet#1
  N16: Part1.SCK, J2.pin7, J4.pin7, ENCODER1.no_name_yet#1
  N17: Part1.A4, J2.pin5, J4.pin5
  N18: Part1.A3, J2.pin4, J4.pin4
  N19: Part1.A2, J2.pin3, J4.pin3
  N20: Part1.A1, J2.pin2, J4.pin2
  N21: Part1.A0, J2.pin1, J4.pin1
  +3V3: Part1.+3V3, J2.pin6, J4.pin6, OLED1.VDD, Q1.C, J5.pin4
  N22: U1.+, U1.-

custom parts:
  Itsy Bitsy 32u4 3V @ 8MHz: What's smaller than a Feather but larger than a Trinket? It's an Itsy Bitsy! Small, powerful, Arduino-compatible - this microcontroller board is perfect when you want something very compact, but still with a bunch of pins. Itsy Bitsy is only 1.4" long by 0.7" wide, but has 6 power pins, 6 analog & digital pins and 17 digital pins. It packs much of the same capability as an Arduino UNO or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
  OLED 128x64 I2C Monochrome Display GND-VDD: OLED 128x64 I2C Monochrome Display. Note: there are two variants of this part, this one is the GND VDD SCK SDA variant. The other is VDD GND SCK SDA. Make sure you select the part that matches your module as using the incorrect part will probably destroy your module! In addition the mounting holes are marked on silkscreen but not by default drilled. If you want drilled mounting holes, copy a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
  Rotary Encoder with Knob: Rotary Encoder with 1/4" Shaft and Knob
  Micro Lipo Charger: Oh so handy, this little lipo charger is so small and easy to use you can keep it on your desk or mount it easily into any project! Simply plug it via any MicroUSB cable into a USB port and a 3.7V/4.2V lithium polymer or lithium ion rechargeable battery into the JST plug on the other end. There are two LEDs - one red and one green. While charging, the red LED is lit. When the battery is fully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
